# Fritzing sketch monitoring tambak ikan bandeng (saved by Fritzing 0.9.3b)

parts:
  U1 = LuaNode32 / ESP32
  Part1 = HC-SR501 Body Sensor Module
  DS2 = DS18B20 1-Wire Temperature Sensor Probe Cable
  S1 = PH meter [package=THT]
  Part2 = Adafruit RFM9x LoRa Radio [part_number="Adafruit #3072 and #3073"]
  BAT1 = BC9VPC [package=bc9vpc]
  U2 = LuaNode32 / ESP32
  Part3 = Adafruit RFM9x LoRa Radio [part_number="Adafruit #3072 and #3073"]

nets:
  N1: U1.VP, Part1.OUT
  N2: U1.D25, S1.pin1
  N3: U1.D27, DS2.DQ
  N4: U1.D14, Part2.RST
  GND: U1.GND, Part2.GND, BAT1.V-
  3V3: U1.3V3, Part2.VIN
  N5: U1.D2, Part2.DIO0
  N6: U1.D5, Part2.EN
  N7: U1.D18, Part2.SCK
  N8: U1.D19, Part2.MISO
  N9: U1.D23, Part2.MOSI
  N10: DS2.VDD, BAT1.V+
  N11: U2.D14, Part3.RST
  3V3_2: U2.3V3, Part3.VIN
  GND_2: U2.GND, Part3.GND
  N12: U2.D2, Part3.DIO0
  N13: U2.D5, Part3.EN
  N14: U2.D18, Part3.SCK
  N15: U2.D19, Part3.MISO
  N16: U2.D23, Part3.MOSI

custom parts:
  LuaNode32 / ESP32: ESP32 based LuaNode32
  HC-SR501 Body Sensor Module: Pyroelectric Infrared PIR Motion Sensor Detector Module
  Adafruit RFM9x LoRa Radio: Sending data over long distances is like magic, and now you can be a magician with this range of powerful and easy-to-use radio modules. Sure, sometimes you want to talk to a computer (a good time to use WiFi) or perhaps communicate with a Phone (choose Bluetooth Low Energy!) but what if you want to send data very far? Most WiFi, Bluetooth, Zigbee and other wireless chipsets use 2.4GHz, which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
